// Logisim project alu.circ as structural Verilog: 12 circuits, main circuit main
module main (
  input  [31:0] X,
  input  [31:0] Y,
  input  [3:0] Switch,
  output Signed_Overflow,
  output Equal,
  output [31:0] Result
);

  wire add_1_over, and_2_out, and_3_out, comparator_2_eq, comparator_3_eq, multiplexer_2_out, or_2_out,
       sub_1_over;
  wire [31:0] add_1_out, addu_1_out, and_1_out, or_1_out, sll_1_out, slt_1_out, sltu_1_out, sra_1_out,
       srl_1_out, sub_1_out, subu_1_out;

  sll sll_1 (.x(X), .y(Y), .out(sll_1_out));
  srl srl_1 (.x(X), .y(Y), .out(srl_1_out));
  sra sra_1 (.x(X), .y(Y), .out(sra_1_out));
  add add_1 (.x(X), .y(Y), .out(add_1_out), .Over(add_1_over));
  addu addu_1 (.x(X), .y(Y), .out(addu_1_out));
  sub sub_1 (.x(X), .y(Y), .out(sub_1_out), .Over(sub_1_over));
  subu subu_1 (.x(X), .y(Y), .out(subu_1_out));
  \and  and_1 (.x(X), .y(Y), .out(and_1_out));
  \or  or_1 (.x(X), .y(Y), .out(or_1_out));
  slt slt_1 (.x(X), .y(Y), .out(slt_1_out));
  sltu sltu_1 (.x(X), .y(Y), .out(sltu_1_out));
  Comparator #(.width(32), .mode("unsigned")) comparator_1 (.a(X), .b(Y), .eq(Equal));  // open: gt, lt
  Comparator #(.width(4)) comparator_2 (.a(Switch), .b(4'b0111), .eq(comparator_2_eq));  // open: gt, lt
  Comparator #(.width(4)) comparator_3 (.a(Switch), .b(4'b0101), .eq(comparator_3_eq));  // open: gt, lt
  or or_2 (or_2_out, and_2_out, and_3_out);
  and and_2 (and_2_out, sub_1_over, comparator_2_eq);
  and and_3 (and_3_out, add_1_over, comparator_3_eq);
  and and_4 (Signed_Overflow, or_2_out, multiplexer_2_out);
  Multiplexer #(.select(4), .width(32)) multiplexer_1 (
    .in0(sll_1_out), .in1(srl_1_out), .in2(sra_1_out), .in5(add_1_out), .in6(addu_1_out), .in7(sub_1_out),
    .in8(subu_1_out), .in9(and_1_out), .in10(or_1_out), .in14(slt_1_out), .in15(sltu_1_out), .out(Result),
    .sel(Switch));  // open: in3, in4, in11, in12, in13, en
  Multiplexer #(.select(4)) multiplexer_2 (
    .in0(1'b0), .in1(1'b0), .in2(1'b0), .in3(1'b0), .in4(1'b0), .in5(1'b1), .in6(1'b0), .in7(1'b1),
    .in8(1'b0), .in9(1'b0), .in10(1'b0), .in11(1'b0), .in12(1'b0), .in13(1'b0), .in14(1'b0), .in15(1'b0),
    .out(multiplexer_2_out), .sel(Switch));  // open: en

  // Other names for the same wires on the sheet: overflow = Signed_Overflow; S[3:0] = Switch

  // Notes on the sheet:
  //   INPUTS to your circuit
  //   DON'T CHANGE THE LOCATIONS OF THE INPUTS AND OUTPUTS!
  //   OUTPUTS from your circuit
endmodule

module sll (
  input  [31:0] x,
  input  [31:0] y,
  output [31:0] out
);

  wire comparator_1_eq, comparator_1_gt, or_1_out;
  wire [31:0] shifter_1_out;

  Comparator #(.width(32)) comparator_1 (.a(x), .b(32'h20), .gt(comparator_1_gt), .eq(comparator_1_eq));  // open: lt
  Shifter #(.width(32)) shifter_1 (.in(y), .\dist (x[4:0]), .out(shifter_1_out));
  or or_1 (or_1_out, comparator_1_gt, comparator_1_eq);
  Multiplexer #(.width(32)) multiplexer_1 (
    .in0(shifter_1_out), .in1({32{1'b0}}), .out(out), .sel(or_1_out));  // open: en
endmodule

module srl (
  input  [31:0] x,
  input  [31:0] y,
  output [31:0] out
);

  wire comparator_1_eq, comparator_1_gt, or_1_out;
  wire [31:0] shifter_1_out;

  Comparator #(.width(32)) comparator_1 (.a(x), .b(32'h20), .gt(comparator_1_gt), .eq(comparator_1_eq));  // open: lt
  Shifter #(.width(32), .shift("lr")) shifter_1 (.in(y), .\dist (x[4:0]), .out(shifter_1_out));
  or or_1 (or_1_out, comparator_1_gt, comparator_1_eq);
  Multiplexer #(.width(32)) multiplexer_1 (
    .in0(shifter_1_out), .in1({32{1'b0}}), .out(out), .sel(or_1_out));  // open: en
endmodule

module sra (
  input  [31:0] x,
  input  [31:0] y,
  output [31:0] out
);

  wire comparator_1_eq, comparator_1_gt, or_1_out;
  wire [31:0] multiplexer_1_out, shifter_1_out;

  Comparator #(.width(32)) comparator_1 (.a(x), .b(32'h20), .gt(comparator_1_gt), .eq(comparator_1_eq));  // open: lt
  Shifter #(.width(32), .shift("ar")) shifter_1 (.in(y), .\dist (x[4:0]), .out(shifter_1_out));
  or or_1 (or_1_out, comparator_1_gt, comparator_1_eq);
  Multiplexer #(.width(32)) multiplexer_1 (
    .in0({32{1'b0}}), .in1({32{1'b1}}), .out(multiplexer_1_out), .sel(x[31]));  // open: en
  Multiplexer #(.width(32)) multiplexer_2 (
    .in0(shifter_1_out), .in1(multiplexer_1_out), .out(out), .sel(or_1_out));  // open: en
endmodule

module add (
  input  [31:0] x,
  input  [31:0] y,
  output [31:0] out,
  output Over
);

  wire and_1_out, and_2_out, and_3_out, and_4_out, not_1_out, not_2_out, not_3_out;

  Adder #(.width(32)) adder_1 (.a(x), .b(y), .out(out));  // open: cin, cout
  and and_1 (and_1_out, x[31], y[31]);
  not not_1 (not_1_out, x[31]);
  and and_2 (and_2_out, not_1_out, not_2_out);
  not not_2 (not_2_out, y[31]);
  not not_3 (not_3_out, out[31]);
  and and_3 (and_3_out, not_3_out, and_1_out);
  and and_4 (and_4_out, out[31], and_2_out);
  or or_1 (Over, and_3_out, and_4_out);
endmodule

module addu (
  input  [31:0] x,
  input  [31:0] y,
  output [31:0] out
);

  Adder #(.width(32)) adder_1 (.a(x), .b(y), .out(out));  // open: cin, cout
endmodule

module sub (
  input  [31:0] x,
  input  [31:0] y,
  output [31:0] out,
  output Over
);

  wire and_1_out, and_2_out, and_3_out, and_4_out, not_1_out, not_2_out, not_3_out;

  Subtractor #(.width(32)) subtractor_1 (.a(x), .b(y), .out(out));  // open: bin, bout
  and and_1 (and_1_out, x[31], not_1_out);
  not not_1 (not_1_out, y[31]);
  not not_2 (not_2_out, x[31]);
  and and_2 (and_2_out, not_2_out, y[31]);
  not not_3 (not_3_out, out[31]);
  and and_3 (and_3_out, not_3_out, and_1_out);
  and and_4 (and_4_out, out[31], and_2_out);
  or or_1 (Over, and_3_out, and_4_out);
endmodule

module subu (
  input  [31:0] x,
  input  [31:0] y,
  output [31:0] out
);

  Subtractor #(.width(32)) subtractor_1 (.a(x), .b(y), .out(out));  // open: bin, bout
endmodule

module \and  (
  input  [31:0] x,
  input  [31:0] y,
  output [31:0] out
);

  assign out = x & y;  // AND_Gate and_1, 32 bits wide
endmodule

module \or  (
  input  [31:0] x,
  input  [31:0] y,
  output [31:0] out
);

  assign out = x | y;  // OR_Gate or_1, 32 bits wide
endmodule

module slt (
  input  [31:0] x,
  input  [31:0] y,
  output [31:0] out
);

  wire comparator_1_lt;

  Comparator #(.width(32)) comparator_1 (.a(x), .b(y), .lt(comparator_1_lt));  // open: gt, eq
  Multiplexer #(.width(32)) multiplexer_1 (
    .in0({32{1'b0}}), .in1(32'h1), .out(out), .sel(comparator_1_lt));  // open: en
endmodule

module sltu (
  input  [31:0] x,
  input  [31:0] y,
  output [31:0] out
);

  wire comparator_1_lt;

  Comparator #(.width(32), .mode("unsigned")) comparator_1 (.a(x), .b(y), .lt(comparator_1_lt));  // open: gt, eq
  Multiplexer #(.width(32)) multiplexer_1 (
    .in0({32{1'b0}}), .in1(32'h1), .out(out), .sel(comparator_1_lt));  // open: en
endmodule
