// Logisim project regfile.circ as structural Verilog: 1 circuit, main circuit main
module main (
  input  [4:0] Read_Register_1,
  input  [4:0] Read_Register_2,
  input  [4:0] Write_Register,
  input  [31:0] Write_Data,
  input  Write_Enable,
  input  Clock,
  output [31:0] s0_Value,
  output [31:0] s1_Value,
  output [31:0] s2_Value,
  output [31:0] ra_Value,
  output [31:0] sp_Value,
  output [31:0] Read_Data_1,
  output [31:0] Read_Data_2
);

  wire clock_1_out, W00, W01, W02, W03, W04, W05, W06, W07, W08, W09, W10, W11, W12, W13, W14, W15, W16, W17,
       W18, W19, W20, W21, W22, W23, W24, W25, W26, W27, W28, W29, W30, W31;
  wire [31:0] in_00, in_01, in_02, in_03, in_04, in_05, in_06, in_07, in_08, in_09, in_10, in_11, in_12,
       in_13, in_14, in_15, in_16, in_17, in_18, in_19, in_20, in_21, in_22, in_23, in_24, in_25, in_26,
       in_27, in_28, in_29, in_30, in_31, out00, out01, out02, out03, out04, out05, out06, out07, out08,
       out09, out10, out11, out12, out13, out14, out15, out19, out20, out21, out22, out23, out24, out25,
       out26, out27, out28, out30;

  Clock clock_1 (.out(clock_1_out));
  Decoder #(.select(5), .disabled(0)) decoder_1 (
    .out0(W00), .out1(W01), .out2(W02), .out3(W03), .out4(W04), .out5(W05), .out6(W06), .out7(W07),
    .out8(W08), .out9(W09), .out10(W10), .out11(W11), .out12(W12), .out13(W13), .out14(W14), .out15(W15),
    .out16(W16), .out17(W17), .out18(W18), .out19(W19), .out20(W20), .out21(W21), .out22(W22), .out23(W23),
    .out24(W24), .out25(W25), .out26(W26), .out27(W27), .out28(W28), .out29(W29), .out30(W30), .out31(W31),
    .sel(Write_Register), .en(Write_Enable));
  Demultiplexer #(.select(5), .width(32)) demultiplexer_1 (
    .out0(in_00), .out1(in_01), .out2(in_02), .out3(in_03), .out4(in_04), .out5(in_05), .out6(in_06),
    .out7(in_07), .out8(in_08), .out9(in_09), .out10(in_10), .out11(in_11), .out12(in_12), .out13(in_13),
    .out14(in_14), .out15(in_15), .out16(in_16), .out17(in_17), .out18(in_18), .out19(in_19), .out20(in_20),
    .out21(in_21), .out22(in_22), .out23(in_23), .out24(in_24), .out25(in_25), .out26(in_26), .out27(in_27),
    .out28(in_28), .out29(in_29), .out30(in_30), .out31(in_31), .in(Write_Data), .sel(Write_Register));  // open: en
  Register #(.width(32)) register_1 (.en(W00), .Q(out00), .clk(Clock));  // open: D, clr
  Register #(.width(32)) register_2 (.D(in_04), .en(W04), .Q(out04), .clk(Clock));  // open: clr
  Register #(.width(32)) register_3 (.D(in_08), .en(W08), .Q(out08), .clk(Clock));  // open: clr
  Register #(.width(32)) register_4 (.D(in_12), .en(W12), .Q(out12), .clk(Clock));  // open: clr
  Register #(.width(32)) register_5 (.D(in_16), .en(W16), .Q(s0_Value), .clk(Clock));  // open: clr
  Register #(.width(32)) register_6 (.D(in_20), .en(W20), .Q(out20), .clk(Clock));  // open: clr
  Register #(.width(32)) register_7 (.D(in_24), .en(W24), .Q(out24), .clk(Clock));  // open: clr
  Register #(.width(32)) register_8 (.D(in_28), .en(W28), .Q(out28), .clk(Clock));  // open: clr
  Register #(.width(32)) register_9 (.D(in_01), .en(W01), .Q(out01), .clk(Clock));  // open: clr
  Register #(.width(32)) register_10 (.D(in_05), .en(W05), .Q(out05), .clk(Clock));  // open: clr
  Register #(.width(32)) register_11 (.D(in_09), .en(W09), .Q(out09), .clk(Clock));  // open: clr
  Register #(.width(32)) register_12 (.D(in_13), .en(W13), .Q(out13), .clk(Clock));  // open: clr
  Register #(.width(32)) register_13 (.D(in_17), .en(W17), .Q(s1_Value), .clk(Clock));  // open: clr
  Register #(.width(32)) register_14 (.D(in_21), .en(W21), .Q(out21), .clk(Clock));  // open: clr
  Register #(.width(32)) register_15 (.D(in_25), .en(W25), .Q(out25), .clk(Clock));  // open: clr
  Register #(.width(32)) register_16 (.D(in_29), .en(W29), .Q(sp_Value), .clk(Clock));  // open: clr
  Register #(.width(32)) register_17 (.D(in_02), .en(W02), .Q(out02), .clk(Clock));  // open: clr
  Register #(.width(32)) register_18 (.D(in_06), .en(W06), .Q(out06), .clk(Clock));  // open: clr
  Register #(.width(32)) register_19 (.D(in_10), .en(W10), .Q(out10), .clk(Clock));  // open: clr
  Register #(.width(32)) register_20 (.D(in_14), .en(W14), .Q(out14), .clk(Clock));  // open: clr
  Register #(.width(32)) register_21 (.D(in_18), .en(W18), .Q(s2_Value), .clk(Clock));  // open: clr
  Register #(.width(32)) register_22 (.D(in_22), .en(W22), .Q(out22), .clk(Clock));  // open: clr
  Register #(.width(32)) register_23 (.D(in_26), .en(W26), .Q(out26), .clk(Clock));  // open: clr
  Register #(.width(32)) register_24 (.D(in_30), .en(W30), .Q(out30), .clk(Clock));  // open: clr
  Register #(.width(32)) register_25 (.D(in_03), .en(W03), .Q(out03), .clk(Clock));  // open: clr
  Register #(.width(32)) register_26 (.D(in_07), .en(W07), .Q(out07), .clk(Clock));  // open: clr
  Register #(.width(32)) register_27 (.D(in_11), .en(W11), .Q(out11), .clk(Clock));  // open: clr
  Register #(.width(32)) register_28 (.D(in_15), .en(W15), .Q(out15), .clk(Clock));  // open: clr
  Register #(.width(32)) register_29 (.D(in_19), .en(W19), .Q(out19), .clk(Clock));  // open: clr
  Register #(.width(32)) register_30 (.D(in_23), .en(W23), .Q(out23), .clk(Clock));  // open: clr
  Register #(.width(32)) register_31 (.D(in_27), .en(W27), .Q(out27), .clk(Clock));  // open: clr
  Register #(.width(32)) register_32 (.D(in_31), .en(W31), .Q(ra_Value), .clk(Clock));  // open: clr
  Multiplexer #(.select(5), .width(32), .enable("false")) multiplexer_1 (
    .in0(out00), .in1(out01), .in2(out02), .in3(out03), .in4(out04), .in5(out05), .in6(out06), .in7(out07),
    .in8(out08), .in9(out09), .in10(out10), .in11(out11), .in12(out12), .in13(out13), .in14(out14),
    .in15(out15), .in16(s0_Value), .in17(s1_Value), .in18(s2_Value), .in19(out19), .in20(out20),
    .in21(out21), .in22(out22), .in23(out23), .in24(out24), .in25(out25), .in26(out26), .in27(out27),
    .in28(out28), .in29(sp_Value), .in30(out30), .in31(ra_Value), .out(Read_Data_1), .sel(Read_Register_1));
  Multiplexer #(.select(5), .width(32), .enable("false")) multiplexer_2 (
    .in0(out00), .in1(out01), .in2(out02), .in3(out03), .in4(out04), .in5(out05), .in6(out06), .in7(out07),
    .in8(out08), .in9(out09), .in10(out10), .in11(out11), .in12(out12), .in13(out13), .in14(out14),
    .in15(out15), .in16(s0_Value), .in17(s1_Value), .in18(s2_Value), .in19(out19), .in20(out20),
    .in21(out21), .in22(out22), .in23(out23), .in24(out24), .in25(out25), .in26(out26), .in27(out27),
    .in28(out28), .in29(sp_Value), .in30(out30), .in31(ra_Value), .out(Read_Data_2), .sel(Read_Register_2));

  // Other names for the same wires on the sheet: clk = Clock; out16[31:0] = s0_Value; out17[31:0] = s1_Value;
  //   out18[31:0] = s2_Value; out29[31:0] = sp_Value; out31[31:0] = ra_Value; read_data1[31:0] = Read_Data_1;
  //   read_data2[31:0] = Read_Data_2; read_reg1[4:0] = Read_Register_1; read_reg2[4:0] = Read_Register_2;
  //   write_en = Write_Enable; write_reg[4:0] = Write_Register

  // Notes on the sheet:
  //   INPUTS to your circuit
  //   DON'T CHANGE THE LOCATIONS OF THE INPUTS AND OUTPUTS!
  //   These are DEBUG/TEST outputs from your circuit.
  //   OUTPUTS from your circuit
endmodule
