// Logisim project cpu.circ as structural Verilog: 1 circuit, main circuit main
// 1
module main (
  input  [31:0] INSTRUCTION,
  input  CLOCK,
  output [31:0] FETCH_ADDRESS,
  output [31:0] s0_Value,
  output [31:0] s1_Value,
  output [31:0] s2_Value,
  output [31:0] ra_Value,
  output [31:0] sp_Value
);

  wire add, addi, addiu, addu, \and , and_6_out, and_7_out, and_8_out, and_9_out, and_11_out, and_12_out,
       and_13_out, and_14_out, andi, beq, bltzal, bne, Branch, comparator_2_eq, comparator_3_eq,
       comparator_4_eq, comparator_5_eq, comparator_6_lt, comparator_7_eq, comparator_8_eq, comparator_9_eq,
       comparator_10_eq, instrBranch, instrJump, isOp1, isOp2, isR, isR1, isR2, j, jal, jr, Jump, KillNext,
       KillThis, link, lui, lw, MemWrite, not_1_out, not_2_out, not_3_out, not_4_out, not_5_out, \or ,
       or_2_out, or_3_out, or_4_out, or_5_out, or_6_out, or_7_out, or_11_out, or_15_out, or_16_out, ori,
       RegWrite, sll, slt, slti, sltiu, sltu, sra, srl, tunnel;
  wire [1:0] ALUSrc, multiplexer_18_out, multiplexer_19_out, multiplexer_20_out;
  wire [3:0] ALUOP, multiplexer_4_out, multiplexer_5_out, multiplexer_6_out, multiplexer_7_out,
       multiplexer_8_out, multiplexer_9_out, multiplexer_10_out, multiplexer_11_out;
  wire [4:0] demultiplexer_1_out0, demultiplexer_1_out1, demultiplexer_2_out0, demultiplexer_2_out1,
       multiplexer_14_out;
  wire [5:0] funct;
  wire [15:6] immediate;
  wire [31:0] ALUR, and_2_out, and_10_out, BDest, instruction2, jAddr, jAddr_OF_TOMORROW, jrAddr,
       linkInstruction, MemOut, multiplexer_1_out, multiplexer_2_out, multiplexer_12_out, multiplexer_15_out,
       multiplexer_16_out, multiplexer_17_out, or_1_out, PC_4, RD2, shifter_1_out;
  wire [31:16] instructionPK;

  Demultiplexer #(.width(5)) demultiplexer_1 (
    .out0(demultiplexer_1_out0), .out1(demultiplexer_1_out1), .in(funct[4:0]), .sel(funct[5]), .en(isR));
  and and_1 (isR2, funct[5], isR);
  Multiplexer #(.width(32), .disabled(0), .enable("false")) multiplexer_1 (
    .in0(PC_4), .in1(BDest), .out(multiplexer_1_out), .sel(Branch));
  assign and_2_out = PC_4 & 32'hf0000000;  // AND_Gate and_2, 32 bits wide
  Shifter #(.width(32)) shifter_1 (
    .in({{17{immediate[15]}}, immediate[14:6], funct}), .\dist (5'b00010), .out(shifter_1_out));
  Comparator #(.width(6)) comparator_1 (.a(instructionPK[31:26]), .b({6{1'b0}}), .eq(isR));  // open: gt, lt
  Decoder #(.select(5), .disabled(0)) decoder_1 (
    .out0(sll), .out2(srl), .out3(sra), .out8(jr), .sel(demultiplexer_1_out0), .en(isR1));  // open: out1, out4, out5, out6, out7, out9, out10, out11, out12, out13, out14, out15, out16, out17, out18, out19, out20, out21, out22, out23, out24, out25, out26, out27, out28, out29, out30, out31
  not not_1 (not_1_out, isR2);
  and and_3 (isR1, not_1_out, isR);
  Register #(.width(32)) PC (.D(multiplexer_2_out), .Q(FETCH_ADDRESS), .clk(CLOCK));  // open: en, clr
  Multiplexer #(.width(32), .disabled(0), .enable("false")) multiplexer_2 (
    .in0(multiplexer_1_out), .in1(jAddr), .out(multiplexer_2_out), .sel(Jump));
  assign or_1_out = and_2_out | {4'b0000, instructionPK[25:16], immediate, funct, 2'b00};  // OR_Gate or_1, 32 bits wide
  Multiplexer #(.width(32), .disabled(0), .enable("false")) multiplexer_3 (
    .in0(or_1_out), .in1(jrAddr), .out(jAddr), .sel(jr));
  Adder #(.width(32)) adder_1 (.a(FETCH_ADDRESS), .b(shifter_1_out), .out(BDest));  // open: cin, cout
  Decoder #(.select(5), .disabled(0)) decoder_2 (
    .out0(add), .out1(addu), .out4(\and ), .out5(\or ), .out10(slt), .out11(sltu),
    .sel(demultiplexer_1_out1), .en(isR2));  // open: out2, out3, out6, out7, out8, out9, out12, out13, out14, out15, out16, out17, out18, out19, out20, out21, out22, out23, out24, out25, out26, out27, out28, out29, out30, out31
  Demultiplexer #(.width(5)) demultiplexer_2 (
    .out0(demultiplexer_2_out0), .out1(demultiplexer_2_out1), .in(instructionPK[30:26]),
    .sel(instructionPK[31]), .en(not_2_out));
  and and_4 (isOp2, instructionPK[31], not_2_out);
  not not_2 (not_2_out, isR);
  Adder #(.width(32)) adder_2 (.a(FETCH_ADDRESS), .b(32'h4), .out(PC_4));  // open: cin, cout
  Decoder #(.select(5), .disabled(0)) decoder_3 (
    .out1(bltzal), .out2(j), .out3(jal), .out4(beq), .out5(bne), .out8(addi), .out9(addiu), .out10(slti),
    .out11(sltiu), .out12(andi), .out13(ori), .out15(lui), .sel(demultiplexer_2_out0), .en(isOp1));  // open: out0, out6, out7, out14, out16, out17, out18, out19, out20, out21, out22, out23, out24, out25, out26, out27, out28, out29, out30, out31
  not not_3 (not_3_out, isOp2);
  and and_5 (isOp1, not_3_out, not_4_out);
  not not_4 (not_4_out, isR);
  or Tweet (RegWrite, srl, sll, sra, add, addu, sltu, sltiu, \or , addi, slt, slti, \and , andi, ori, lui, lw, addiu);
  Decoder #(.select(5), .disabled(0)) decoder_4 (
    .out3(lw), .out11(MemWrite), .sel(demultiplexer_2_out1), .en(isOp2));  // open: out0, out1, out2, out4, out5, out6, out7, out8, out9, out10, out12, out13, out14, out15, out16, out17, out18, out19, out20, out21, out22, out23, out24, out25, out26, out27, out28, out29, out30, out31
  or or_2 (or_2_out, addu, addiu);
  or or_3 (or_3_out, add, addi);
  or or_4 (or_4_out, \and , andi);
  or or_5 (or_5_out, \or , ori);
  or or_6 (or_6_out, slti, bltzal, slt);
  or or_7 (or_7_out, sltiu, sltu);
  Multiplexer #(.width(4), .disabled(0), .enable("false")) multiplexer_4 (
    .in0(4'b0000), .in1(4'b0001), .out(multiplexer_4_out), .sel(srl));
  Multiplexer #(.width(4), .disabled(0), .enable("false")) multiplexer_5 (
    .in0(4'b0000), .in1(4'b0010), .out(multiplexer_5_out), .sel(sra));
  Multiplexer #(.width(4), .disabled(0), .enable("false")) multiplexer_6 (
    .in0(4'b0000), .in1(4'b0110), .out(multiplexer_6_out), .sel(or_2_out));
  Multiplexer #(.width(4), .disabled(0), .enable("false")) multiplexer_7 (
    .in0(4'b0000), .in1(4'b0101), .out(multiplexer_7_out), .sel(or_3_out));
  Multiplexer #(.width(4), .disabled(0), .enable("false")) multiplexer_8 (
    .in0(4'b0000), .in1(4'b1001), .out(multiplexer_8_out), .sel(or_4_out));
  Multiplexer #(.width(4), .disabled(0), .enable("false")) multiplexer_9 (
    .in0(4'b0000), .in1(4'b1010), .out(multiplexer_9_out), .sel(or_5_out));
  Multiplexer #(.width(4), .disabled(0), .enable("false")) multiplexer_10 (
    .in0(4'b0000), .in1(4'b1110), .out(multiplexer_10_out), .sel(or_6_out));
  Multiplexer #(.width(4), .disabled(0), .enable("false")) multiplexer_11 (
    .in0(4'b0000), .in1(4'b1111), .out(multiplexer_11_out), .sel(or_7_out));
  and and_6 (and_6_out, beq, tunnel);
  and and_7 (and_7_out, bne, ~tunnel);  // AND_Gate
  or or_8 (Branch, and_6_out, and_7_out, and_8_out);
  and and_8 (and_8_out, bltzal, ALUR[0]);
  or or_9 (Jump, jr, jal, j);
  or or_10 (KillNext, Jump, Branch);
  D_Flip_Flop Kill (.clk(CLOCK), .D(KillNext), .Q(KillThis), .preset(1'b0), .en(1'b1), .reset(1'b0));  // open: Qn
  Multiplexer #(.width(32), .disabled(0), .enable("false")) multiplexer_12 (
    .in0({32{1'b0}}), .in1(linkInstruction), .out(multiplexer_12_out), .sel(link));
  assign ALUOP = multiplexer_4_out | multiplexer_5_out | multiplexer_6_out | multiplexer_7_out | multiplexer_8_out | multiplexer_9_out | multiplexer_10_out | multiplexer_11_out;  // OR_Gate Octopussy, 4 bits wide
  Multiplexer #(.width(32), .disabled(0), .enable("false")) multiplexer_13 (
    .in0(instruction2), .in1(multiplexer_12_out), .out({instructionPK, immediate, funct}), .sel(KillThis));
  Register #(.width(32)) Instruction_delay (.D(INSTRUCTION), .Q(instruction2), .clk(CLOCK));  // open: en, clr
  Register #(.width(32)) register_1 (
    .D({16'h341f, FETCH_ADDRESS[15:0]}), .Q(linkInstruction), .clk(CLOCK));  // open: en, clr
  and and_9 (and_9_out, bltzal, ALUR[0]);
  or or_11 (or_11_out, and_9_out, jal);
  Register #(.width(1)) register_2 (.D(or_11_out), .Q(link), .clk(CLOCK));  // open: en, clr
  Multiplexer #(.width(5), .disabled(0), .enable("false")) multiplexer_14 (
    .in0(instructionPK[20:16]), .in1(immediate[15:11]), .out(multiplexer_14_out), .sel(isR));
  Multiplexer #(.width(32), .disabled(0), .enable("false")) multiplexer_15 (
    .in0(ALUR), .in1(MemOut), .out(multiplexer_15_out), .sel(lw));
  regfile_main main_1 (
    .Read_Register_1(instructionPK[25:21]), .Read_Register_2(instructionPK[20:16]),
    .Write_Register(multiplexer_14_out), .Write_Data(multiplexer_16_out), .Write_Enable(RegWrite),
    .Clock(CLOCK), .Read_Data_1(jrAddr), .Read_Data_2(RD2), .s0_Value(s0_Value), .s1_Value(s1_Value),
    .s2_Value(s2_Value), .ra_Value(ra_Value), .sp_Value(sp_Value));
  Multiplexer #(.width(32), .disabled(0), .enable("false")) multiplexer_16 (
    .in0(multiplexer_15_out), .in1({immediate, funct, {16{1'b0}}}), .out(multiplexer_16_out), .sel(lui));
  Comparator #(.width(6)) comparator_2 (.a(INSTRUCTION[31:26]), .b({6{1'b0}}), .eq(comparator_2_eq));  // open: gt, lt
  Comparator #(.width(6)) comparator_3 (.a(INSTRUCTION[31:26]), .b(6'b000100), .eq(comparator_3_eq));  // open: gt, lt
  Comparator #(.width(6)) comparator_4 (.a(INSTRUCTION[31:26]), .b(6'b000101), .eq(comparator_4_eq));  // open: gt, lt
  Comparator #(.width(6)) comparator_5 (.a(INSTRUCTION[31:26]), .b(6'b000001), .eq(comparator_5_eq));  // open: gt, lt
  Comparator #(.width(16)) comparator_6 (.a(INSTRUCTION[15:0]), .b({16{1'b0}}), .lt(comparator_6_lt));  // open: gt, eq
  assign jAddr_OF_TOMORROW = {4'b0000, INSTRUCTION[25:0], 2'b00} | and_10_out;  // OR_Gate or_12, 32 bits wide
  assign and_10_out = PC_4 & 32'hf0000000;  // AND_Gate and_10, 32 bits wide
  Comparator #(.width(5)) comparator_7 (
    .a(INSTRUCTION[20:16]), .b(INSTRUCTION[25:21]), .eq(comparator_7_eq));  // open: gt, lt
  alu_main main_2 (
    .Switch(ALUOP), .X(jrAddr), .Equal(tunnel), .Result(ALUR), .Y(multiplexer_17_out));  // open: Signed_Overflow
  Multiplexer #(.select(2), .width(32), .disabled(0), .enable("false")) multiplexer_17 (
    .in0(RD2), .in1({{17{immediate[15]}}, immediate[14:6], funct}), .in2({{16{1'b0}}, immediate, funct}),
    .in3({32{1'b0}}), .out(multiplexer_17_out), .sel(ALUSrc));
  Comparator #(.width(6)) comparator_8 (.a(INSTRUCTION[31:26]), .b(6'b000010), .eq(comparator_8_eq));  // open: gt, lt
  Comparator #(.width(6)) comparator_9 (.a(INSTRUCTION[31:26]), .b(6'b000011), .eq(comparator_9_eq));  // open: gt, lt
  Comparator #(.width(6)) comparator_10 (.a(INSTRUCTION[5:0]), .b(6'b001000), .eq(comparator_10_eq));  // open: gt, lt
  and and_11 (and_11_out, comparator_10_eq, comparator_2_eq);
  and and_12 (and_12_out, comparator_3_eq, comparator_7_eq);
  and and_13 (and_13_out, ~comparator_7_eq, comparator_4_eq);  // AND_Gate
  and and_14 (and_14_out, comparator_5_eq, comparator_6_lt);
  or or_13 (instrBranch, and_12_out, and_13_out, and_14_out);
  // mem_main main_3: pin names not known; wires that end beside it: ALUR, RD2, MemWrite, CLOCK, MemOut
  or or_14 (instrJump, comparator_8_eq, comparator_9_eq, and_11_out);
  Multiplexer #(.width(2), .disabled(0), .enable("false")) multiplexer_18 (
    .in0(2'b00), .in1(2'b01), .out(multiplexer_18_out), .sel(not_5_out));
  or or_15 (or_15_out, isR, bne, beq, ori, andi);
  not not_5 (not_5_out, or_15_out);
  Multiplexer #(.width(2), .disabled(0), .enable("false")) multiplexer_19 (
    .in0(2'b00), .in1(2'b10), .out(multiplexer_19_out), .sel(or_16_out));
  or or_16 (or_16_out, ori, andi);
  Multiplexer #(.width(2), .disabled(0), .enable("false")) multiplexer_20 (
    .in0(2'b00), .in1(2'b11), .out(multiplexer_20_out), .sel(bltzal));
  assign ALUSrc = multiplexer_18_out | multiplexer_19_out | multiplexer_20_out;  // OR_Gate or_17, 2 bits wide

  // Other names for the same wires on the sheet: fetch_addr[31:0] = FETCH_ADDRESS; PC[31:0] = FETCH_ADDRESS;
  //   clk = CLOCK; instrRT[4:0] = INSTRUCTION[20:16]; instrRS[4:0] = INSTRUCTION[25:21];
  //   op[5:0] = instructionPK[31:26]; RegDest = isR; MemRead = lw; MemToReg = lw;
  //   preAddr[27:2] = {instructionPK[25:16], immediate, funct}; rt[4:0] = instructionPK[20:16];
  //   rs[4:0] = instructionPK[25:21]; ra[31:0] = ra_Value; s0[31:0] = s0_Value; s1[31:0] = s1_Value;
  //   s2[31:0] = s2_Value; sp[31:0] = sp_Value; sw = MemWrite; immediate[5:0] = funct;
  //   instructionPK[15:0] = {immediate, funct}; SEI[31:0] = {{17{immediate[15]}}, immediate[14:6], funct};
  //   upperImmediate[31:16] = {immediate, funct}; ZEI[15:0] = {immediate, funct}; shamt[4:0] = immediate[10:6];
  //   rd[4:0] = immediate[15:11]

  // Notes on the sheet:
  //   Output
  //   These are outputs/inputs from run.circ
  //   Inputs
  //   These are DEBUG/TEST outputs from your circuit.
  //   TOMORROWLAND
  //   beq
  //   bne
  //   blitzal
endmodule
