// Logisim project alu-sll.circ as structural Verilog: 1 circuit, main circuit main
module main (
  output Halt,
  output [7:0] Test_num,
  output Signed_Overflow,
  output Equal,
  output [31:0] Result
);

  wire clock_1_out, comparator_1_eq;
  wire [3:0] rom_3_data;
  wire [7:0] adder_1_out;
  wire [15:0] undriven;
  wire [31:0] rom_1_data, rom_2_data;

  Clock clock_1 (.out(clock_1_out));
  Adder adder_1 (.a(8'h1), .b(Test_num), .out(adder_1_out));  // open: cin, cout
  Register register_1 (.D(adder_1_out), .Q(Test_num), .clk(clock_1_out));  // open: en, clr
  Comparator #(.width(16)) comparator_1 (.a(16'h4), .b(undriven), .eq(comparator_1_eq));  // open: gt, lt
  ROM #(.dataWidth(32)) rom_1 (.addr(Test_num), .data(rom_1_data));  // open: sel
  ROM #(.dataWidth(32)) rom_2 (.addr(Test_num), .data(rom_2_data));  // open: sel
  ROM #(.dataWidth(4)) rom_3 (.addr(Test_num), .data(rom_3_data));  // open: sel
  alu_main main_1 (
    .Switch(rom_3_data), .X(rom_1_data), .Equal(Equal), .Result(Result), .Signed_Overflow(Signed_Overflow),
    .Y(rom_2_data));

  // Notes on the sheet:
  //   contents of rom_1 (hex, n*v repeats v):
  //   0 1 2 8
  //   contents of rom_2 (hex, n*v repeats v):
  //   4*1
  //   YOUR ALU SHOULD FIT HERE
  //   There should be no blue/red wires here, and the result shouldn't be x's.
endmodule
